# Fritzing sketch Fritzing (saved by Fritzing 0.9.3b)

parts:
  Raspberry_Pi_1 = Raspberry Pi 3 [part_number=RPI-3-V1.2]
  U2 = TOUCH [package=touch2]

nets:
  N1: Raspberry_Pi_1.GPIO2, U2.SIG
  GND: Raspberry_Pi_1.GND, U2.GND
  5V: Raspberry_Pi_1.5V, U2.VCC

notes:
  Blue - GND
  Green - VCC
  Yellow - SIG

custom parts:
  TOUCH: Electrode for resistive touch detection
